// Logisim project nand_complete_proof.circ as structural Verilog: 1 circuit, main circuit main
module main (
  input  A,
  input  A_2,
  input  B,
  input  A_3,
  input  B_2,
  output nA,
  output A_B,
  output A_B_2
);

  wire nand_2_out, nand_3_out, nand_4_out;

  nand nand_1 (nA, A, A);
  nand nand_2 (nand_2_out, A_2, B);
  nand nand_3 (nand_3_out, A_3, A_3);
  nand nand_4 (nand_4_out, B_2, B_2);
  nand nand_5 (A_B_2, nand_3_out, nand_4_out);
  nand nand_6 (A_B, nand_2_out, nand_2_out);

  // Notes on the sheet:
  //   NAND->NOT
  //   NAND->AND
  //   NAND->OR
  //   A
  //   A
  //   ~(A·A)=~A
  //   ~(A·B)
  //   ~A
  //   ~B
  //   ~(A·B)
  //   ~(A·B)
  //   ~(~A&~B)=A+B
endmodule
